# Fritzing sketch Temp (saved by Fritzing 0.9.3b)
breadboards: 1

parts:
  U1 = MLX90614 [package=to-39]
  Raspberry_Pi_1 = Raspberry Pi B+

nets:
  N1: U1.SCL_VZ, Raspberry_Pi_1.GPIO2
  N2: U1.PWM_SDA, Raspberry_Pi_1.GPIO3
  VDD: U1.VDD, Raspberry_Pi_1.5V
  VSS: U1.VSS, Raspberry_Pi_1.GND

// code stored in the sketch: Lectura.bas
from smbus2 import SMBus
from mlx90614 import MLX90614
import RPi.GPIO as GPIO
from time import sleep

GPIO.setmode(GPIO.BOARD)

push= #pin GPIO del boton
GPIO.setup(push, GPIO.IN)

def lectura_boton():
    if GPIO.input(push):
        return False
    else:
        return True

while True:
    #Se establece la comunicacion con el sensor
    bus = SMBus(1)
    dir= #pin GPIO del sensor
    sensor = MLX90614(bus, address=dir)
    #Se cargan los datos leidos por el sensor
    boton=lectura_boton()
    if boton is True:
        print sensor.get_amb_temp()
        print sensor.get_obj_temp()
        boton=False
    sleep(0.1)
    bus.close()
